# Fritzing sketch Alohomora-3FA_Schematic_Fritzing (saved by Fritzing 0.9.3b)
perfboards: 2

parts:
  Componente1 = Arduino Nano (Rev3.0) (ICSP)
  Componente2 = RFID-RC522-v2
  J1 = Basic Servo
  R1 = Resistor [tolerance=±5% resistance=330 package=THT]
  LED1 = LED - 5mm [color="Red (633nm)" package="5 mm [THT]"]
  J2 = Piezo Speaker
  KEYPAD1 = Membrane Matrix Keypad
  U1 = NodeMCU V3.0
  J6 = Screw terminal - 2 pins [package=THT]
  J7 = Screw terminal - 2 pins [package=THT]
  F1 = FUSE [package=fuse_5mm]
  JP1 = Header 1 [package=1x01_offset]
  JP2 = Header 1 [package=1x01_offset]
  JP3 = Header 1 [package=1x01_offset]  # not connected
  JP4 = Header 1 [package=1x01_offset]
  D3 = Rectifier Diode [part_number=1N4007 package="300 mil [THT]"]
  D4 = Rectifier Diode [part_number=1N4001 package="300 mil [THT]"]
  J8 = screw terminal, 6 pins
  J9 = screw terminal, 6 pins
  C1 = Electrolytic Capacitor [capacitance=1µF package="100 mil [THT, electrolytic]"]
  JP5 = Header 1 [package=1x01_offset]
  JP10 = Header 1 [package=1x01_offset]
  U6 = V_REG_LD1117VXX [package=78xxl]
  C3 = Electrolytic Capacitor [capacitance=10µF voltage=16V package="100 mil [THT, electrolytic]"]
  C4 = Electrolytic Capacitor [capacitance=22µF package="100 mil [THT, electrolytic]"]  # not connected
  C5 = Ceramic Capacitor [capacitance=100nF package="100 mil [THT, multilayer]"]
  VCC1 = 4 x AAA Battery Mount
  VCC2 = 4 x AAA Battery Mount
  U8 = 941H-2C-5D [package=relay-5v]
  Reg1 = DC-DC CONVERTER [part_number=80633 package=dc-dc_converter]
  J16 = screw terminal, 4 pins
  J17 = screw terminal, 6 pins
  J15 = screw terminal, 6 pins
  J18 = screw terminal, 4 pins
  LED3 = LED - 5mm [color="Green (570nm)" package="5 mm [THT]"]
  LED4 = LED - 5mm [color="Red (633nm)" package="5 mm [THT]"]
  R3 = Resistor [tolerance=±5% resistance=220 package=THT]
  R4 = Resistor [tolerance=±5% resistance=220 package=THT]
  Componente3 = Logic Level Converter
  D5 = Rectifier Diode [part_number=1N4001 package="300 mil [THT]"]
  D6 = Rectifier Diode [part_number=1N4001 package="300 mil [THT]"]
  D7 = Rectifier Diode [part_number=1N4001 package="300 mil [THT]"]
  R5 = Resistor [tolerance=±5% resistance=100 package=THT]

nets:
  N1: Componente1.GND, J2.pin1, J17.pin3
  N2: Componente1.D2, R5.Pin_1
  N3: Componente1.D3, J1.pulse
  N4: Componente1.D5, Componente3.RX_HV
  N5: Componente1.D6, Componente3.TX_HV
  N6: Componente1.D7, R4.Pin_1
  N7: Componente1.D8, R3.Pin_1
  N8: Componente1.D9, Componente2.RST
  N9: Componente1.D10, Componente2.SDA
  N10: Componente1.D11/MOSI, Componente2.MOSI
  N11: Componente1.D12/MISO, Componente2.MISO
  N12: Componente1.VIN, D6.cathode
  N13: Componente1.D13/SCK, Componente2.SCK
  N14: Componente2.GND, J16.pin3
  N15: Componente2.3.3V, J18.pin3
  N16: J1.gnd, J17.pin2
  N17: J1.vcc, J15.pin2
  N18: R1.Pin_0, JP1.1, J9.pin1, J9.pin6, C1.+, U8.9
  N19: R1.Pin_1, LED1.anode
  N20: LED1.cathode, J8.pin6, C1.-, JP5.1, U8.8
  N21: KEYPAD1.1, U1.D1
  N22: KEYPAD1.2, U1.D2
  N23: KEYPAD1.3, U1.D3
  N24: KEYPAD1.4, U1.D4
  N25: KEYPAD1.5, U1.D0
  N26: KEYPAD1.6, U1.D5
  N27: KEYPAD1.7, U1.D6
  N28: U1.D8, Componente3.TX_LV
  N29: U1.RX, Componente3.RX_LV
  N30: U1.Vin, D5.cathode
  N31: U1.GND, J17.pin5
  N32: J6.pin1, J7.pin2, VCC1.+
  N33: J6.pin2, F1.1, JP4.1
  N34: J7.pin1, JP2.1, D3.anode, VCC2.-, U8.1, U8.4, U8.6
  N35: F1.2, D4.anode
  N36: D3.cathode, D4.cathode, JP10.1, U8.11, U8.13, U8.16
  N37: J8.pin1, J8.pin2
  N38: J9.pin4, Reg1.IN+
  N39: U6.OUT, C5.0, J18.pin1
  N40: U6.IN, C3.+, J15.pin6
  N41: VCC1.-, VCC2.+
  N42: Reg1.OUT-, J17.pin1
  N43: Reg1.OUT+, D7.anode
  N44: J16.pin1, J17.pin6
  N45: J16.pin4, J17.pin4, Componente3.GND
  N46: J15.pin1, D7.cathode
  N47: J15.pin3, D6.anode
  N48: J15.pin4, Componente3.HV
  N49: J15.pin5, D5.anode
  N50: J18.pin4, Componente3.LV
  N51: LED3.cathode, LED4.cathode
  N52: LED3.anode, R4.Pin_0
  N53: LED4.anode, R3.Pin_0

notes:
  +
  -
  INPUT 12 volt
  12 Volt - Voltage divider- from sv1afn
  Switch
  On-Off
  OUT +12V
  OUT - ground
  By-Pass
  Step-down 12V to 5V
  LM1117-3,3
  5 to 3,3 Volt - step down
  12 Volt
  5 Volt
  3,3 Volt
  VCC 3,3
  Reset
  GND
  MISO
  MOSI
  SCK
  SS
  Legend
  - 5V +
  + 3,3 V -

custom parts:
  RFID-RC522-v2: A simple China made RFID-RC522 Reader; do check the pin labels, as this is a MFRC522 based clone.
  Membrane Matrix Keypad: Membrane Matrix 3x4 Keypad
  NodeMCU V3.0: ESP8266 based NodeMCU
  941H-2C-5D: DPDT Relay - 2 Form C
  DC-DC CONVERTER: WYHP 5A constant current/voltage manufactured by Shenzhen Weiyapuhua Technology Co., Ltd
